# Fritzing sketch esp32BlinkingLEDv2 (saved by Fritzing 0.9.5d)
circuit board: 8.66732cm x 4.71414cm
breadboards: 1

parts:
  M1 = ESP32-S3-DevKitC-1-N8R8-v1 [part_number=ESP32-S3-DevKitC-1-N8R8-v1]
  LED1 = LED - 5mm [color="Red (633nm)" package="5 mm [THT]"]
  R1 = Resistor [tolerance=±5% resistance=220 package=THT]
  S1 = Pushbutton [package="[SMD]"]

nets:
  N1: M1.pin_1, M1.pin_2
  N2: M1.pin_5, LED1.anode
  N3: M1.pin_19, S1.Pin_3, S1.Pin_4
  N4: M1.pin_22, M1.pin_23, M1.pin_24, M1.pin_44, R1.Pin_0, S1.Pin_1, S1.Pin_2
  N5: LED1.cathode, R1.Pin_1

custom parts:
  ESP32-S3-DevKitC-1-N8R8-v1: ESP32-S3-DevKitC-1-N8R8-v1 This module is 44pins long (2x22) and 11 pins width.
