# Fritzing sketch circuit-v1 (saved by Fritzing 0.9.5d)
circuit board: 8.66732cm x 4.71414cm
breadboards: 1

parts:
  part = ESP32-S3-DevKitC-1-N8R8-v1 [part_number=ESP32-S3-DevKitC-1-N8R8-v1]
  LED1 = LED - 5mm [color="Red (633nm)" package="5 mm [THT]"]
  R1 = Resistor [tolerance=±5% resistance=220 package=THT]

nets:
  N1: part.pin_1, part.pin_2
  N2: part.pin_5, LED1.anode
  N3: part.pin_22, part.pin_23, part.pin_24, part.pin_44, R1.Pin_0
  N4: LED1.cathode, R1.Pin_1

custom parts:
  ESP32-S3-DevKitC-1-N8R8-v1: ESP32-S3-DevKitC-1-N8R8-v1 This module is 44pins long (2x22) and 11 pins width.
